// Digital circuit even-top.dig as structural Verilog
module even_top (
  input  [2:0] N,
  output even,
  output odd
);

  even_bits even_bits_1 (.n_0(N[0]), .n_1(N[1]), .n_2(N[2]), .even(even), .odd(odd));
endmodule
